# Fritzing sketch solenoid_valve (saved by Fritzing 0.9.3b)
breadboards: 1

parts:
  부품1 = Arduino Uno (Rev3) - ICSP
  KY-1 = Keyes Relay [package=THT]
  VALVE1 = Plastic Solenoid Valve
  Power_plug1 = Power plug

nets:
  N1: 부품1.D4, KY-1.ground
  N2: 부품1.5V, KY-1.signal
  N3: 부품1.GND, KY-1.power
  N4: KY-1.NC, Power_plug1.GND
  N5: KY-1.NO, VALVE1.no_name_yet#1
  N6: VALVE1.no_name_yet#2, Power_plug1.VCC

custom parts:
  Keyes Relay: The Keyes 5V relay module is suitable for SCM development, home appliance control. It uses a 5V~12V TIL control signal which can control DC / AC signal.
